# Fritzing sketch ElectronicsLayout (saved by Fritzing 0.9.3b)
breadboards: 1

parts:
  Part1 = Arduino Uno (Rev3)
  LED1 = LED - 5mm [color="Green (555nm)" package="5 mm [THT]"]
  LED2 = LED - 5mm [color="Red (633nm)" package="5 mm [THT]"]
  S2 = Round Pushbutton
  S3 = Round Pushbutton  # not connected
  S4 = Round Pushbutton
  S5 = Round Pushbutton
  S6 = Round Pushbutton

nets:
  N1: Part1.D10_PWM/SS, LED2.cathode
  N2: Part1.D12/MISO, LED1.cathode
  N3: Part1.D5_PWM, S2.leg0, S2.leg1, S4.leg0, S4.leg1, S5.leg0, S5.leg1, S6.leg0
